// Logisim project alu.circ as structural Verilog: 1 circuit, main circuit main
module main (
  input  [31:0] X,
  input  [31:0] Y,
  input  [3:0] Switch,
  output Signed_Overflow,
  output Equal,
  output [31:0] Result
);

  wire add_co, and_2_out, and_3_out, and_4_out, and_5_out, comparator_1_lt, comparator_2_lt, comparator_3_lt,
       comparator_4_lt, comparator_5_gt, comparator_6_gt, comparator_7_gt, comparator_8_lt, comparator_9_gt,
       comparator_10_lt, comparator_11_lt, comparator_12_lt, comparator_13_gt, comparator_14_gt, sub_co;
  wire [4:0] bit_extender_1_out, bit_extender_2_out, bit_extender_3_out;
  wire [31:0] add_result, adder_2_out, and_1_out, bit_extender_4_out, bit_extender_5_out, bit_extender_6_out,
       bit_extender_7_out, bit_extender_8_out, bit_extender_9_out, bit_extender_10_out, bit_extender_11_out,
       bit_extender_12_out, bit_extender_13_out, bit_extender_14_out, bit_extender_15_out,
       bit_extender_16_out, bit_extender_17_out, or_1_out, shifter_1_out, shifter_2_out, shifter_3_out,
       sub_result, subtractor_2_out;

  Shifter #(.width(32)) shifter_1 (.in(Y), .\dist (bit_extender_1_out), .out(shifter_1_out));
  Bit_Extender #(.in_width(32), .out_width(5)) bit_extender_1 (.in(X), .out(bit_extender_1_out));
  Shifter #(.width(32), .shift("lr")) shifter_2 (.in(Y), .\dist (bit_extender_2_out), .out(shifter_2_out));
  Bit_Extender #(.in_width(32), .out_width(5)) bit_extender_2 (.in(X), .out(bit_extender_2_out));
  Shifter #(.width(32), .shift("ar")) shifter_3 (.in(Y), .\dist (bit_extender_3_out), .out(shifter_3_out));
  Bit_Extender #(.in_width(32), .out_width(5)) bit_extender_3 (.in(X), .out(bit_extender_3_out));
  Adder #(.width(32)) adder_1 (.a(Y), .b(X), .out(add_result));  // open: cin, cout
  Adder #(.width(32)) adder_2 (.a(Y), .b(X), .out(adder_2_out));  // open: cin, cout
  Subtractor #(.width(32)) subtractor_1 (.a(X), .b(Y), .out(sub_result));  // open: bin, bout
  Subtractor #(.width(32)) subtractor_2 (.a(X), .b(Y), .out(subtractor_2_out));  // open: bin, bout
  Comparator #(.width(32)) comparator_1 (.a(X), .b(Y), .lt(comparator_1_lt));  // open: gt, eq
  Comparator #(.width(32), .mode("unsigned")) comparator_2 (
    .a(X), .b(Y), .eq(Equal), .lt(comparator_2_lt));  // open: gt
  assign and_1_out = Y & X;  // AND_Gate and_1, 32 bits wide
  assign or_1_out = Y | X;  // OR_Gate or_1, 32 bits wide
  assign bit_extender_4_out = {{31{1'b0}}, comparator_1_lt};  // Bit_Extender bit_extender_4
  assign bit_extender_5_out = {{31{1'b0}}, comparator_2_lt};  // Bit_Extender bit_extender_5
  Multiplexer #(.select(4), .width(32)) multiplexer_1 (
    .in0(shifter_1_out), .in1(shifter_2_out), .in2(shifter_3_out), .in5(add_result), .in6(adder_2_out),
    .in7(sub_result), .in8(subtractor_2_out), .in9(and_1_out), .in10(or_1_out), .in11(bit_extender_4_out),
    .in12(bit_extender_5_out), .out(Result), .sel(Switch));  // open: in3, in4, in13, in14, in15, en
  assign bit_extender_6_out = {{31{1'b0}}, 1'b0};  // Bit_Extender bit_extender_6
  assign bit_extender_7_out = {{31{1'b0}}, 1'b0};  // Bit_Extender bit_extender_7
  assign bit_extender_8_out = {{31{1'b0}}, 1'b0};  // Bit_Extender bit_extender_8
  assign bit_extender_9_out = {{31{1'b0}}, 1'b0};  // Bit_Extender bit_extender_9
  assign bit_extender_10_out = {{31{1'b0}}, 1'b0};  // Bit_Extender bit_extender_10
  assign bit_extender_11_out = {{31{1'b0}}, 1'b0};  // Bit_Extender bit_extender_11
  Comparator #(.width(32)) comparator_3 (.a(X), .b(bit_extender_6_out), .lt(comparator_3_lt));  // open: gt, eq
  Comparator #(.width(32)) comparator_4 (.a(Y), .b(bit_extender_7_out), .lt(comparator_4_lt));  // open: gt, eq
  Comparator #(.width(32)) comparator_5 (.a(add_result), .b(bit_extender_8_out), .gt(comparator_5_gt));  // open: eq, lt
  Comparator #(.width(32)) comparator_6 (.a(X), .b(bit_extender_9_out), .gt(comparator_6_gt));  // open: eq, lt
  Comparator #(.width(32)) comparator_7 (.a(Y), .b(bit_extender_10_out), .gt(comparator_7_gt));  // open: eq, lt
  Comparator #(.width(32)) comparator_8 (
    .a(add_result), .b(bit_extender_11_out), .lt(comparator_8_lt));  // open: gt, eq
  and and_2 (and_2_out, comparator_3_lt, comparator_4_lt, comparator_5_gt);
  and and_3 (and_3_out, comparator_6_gt, comparator_7_gt, comparator_8_lt);
  Multiplexer #(.select(4)) multiplexer_2 (
    .in0(1'b0), .in1(1'b0), .in2(1'b0), .in3(1'b0), .in4(1'b0), .in5(add_co), .in6(1'b0), .in7(sub_co),
    .in8(1'b0), .in9(1'b0), .in10(1'b0), .in11(1'b0), .in12(1'b0), .in13(1'b0), .in14(1'b0), .in15(1'b0),
    .out(Signed_Overflow), .sel(Switch));  // open: en
  or or_2 (add_co, and_2_out, and_3_out);
  assign bit_extender_12_out = {{31{1'b0}}, 1'b0};  // Bit_Extender bit_extender_12
  assign bit_extender_13_out = {{31{1'b0}}, 1'b0};  // Bit_Extender bit_extender_13
  assign bit_extender_14_out = {{31{1'b0}}, 1'b0};  // Bit_Extender bit_extender_14
  assign bit_extender_15_out = {{31{1'b0}}, 1'b0};  // Bit_Extender bit_extender_15
  assign bit_extender_16_out = {{31{1'b0}}, 1'b0};  // Bit_Extender bit_extender_16
  assign bit_extender_17_out = {{31{1'b0}}, 1'b0};  // Bit_Extender bit_extender_17
  Comparator #(.width(32)) comparator_9 (.a(X), .b(bit_extender_12_out), .gt(comparator_9_gt));  // open: eq, lt
  Comparator #(.width(32)) comparator_10 (.a(Y), .b(bit_extender_13_out), .lt(comparator_10_lt));  // open: gt, eq
  Comparator #(.width(32)) comparator_11 (
    .a(sub_result), .b(bit_extender_14_out), .lt(comparator_11_lt));  // open: gt, eq
  Comparator #(.width(32)) comparator_12 (.a(X), .b(bit_extender_15_out), .lt(comparator_12_lt));  // open: gt, eq
  Comparator #(.width(32)) comparator_13 (.a(Y), .b(bit_extender_16_out), .gt(comparator_13_gt));  // open: eq, lt
  Comparator #(.width(32)) comparator_14 (
    .a(sub_result), .b(bit_extender_17_out), .gt(comparator_14_gt));  // open: eq, lt
  and and_4 (and_4_out, comparator_9_gt, comparator_10_lt, comparator_11_lt);
  and and_5 (and_5_out, comparator_12_lt, comparator_13_gt, comparator_14_gt);
  or or_3 (sub_co, and_4_out, and_5_out);

  // Other names for the same wires on the sheet: overflow = Signed_Overflow; S[3:0] = Switch

  // Notes on the sheet:
  //   INPUTS to your circuit
  //   DON'T CHANGE THE LOCATIONS OF THE INPUTS AND OUTPUTS!
  //   OUTPUTS from your circuit
  //   These three parts together form the signed overflow detection unit.
  //   Reporting overflow when either ++ produce -, or -- produces +
endmodule
