// Logisim project run.circ as structural Verilog: 1 circuit, main circuit main
module main (
  output [15:0] _1_Value,
  output [15:0] _2_Value,
  output [15:0] _3_Value,
  output [15:0] _6_i_e__ra_Value,
  output [15:0] _7_i_e__sp_Value,
  output [31:0] Time_Step,
  output [31:0] Requested_Address,
  output [15:0] Requested_Instruction,
  output [15:0] Requested_Instruction_2,
  output [31:0] out_10
);

  wire clock_1_out, comparator_1_eq, comparator_2_eq, comparator_3_eq, comparator_4_eq, comparator_5_eq,
       comparator_6_eq, comparator_8_eq, comparator_9_eq, comparator_10_eq, comparator_11_eq,
       comparator_12_eq, comparator_13_eq, comparator_14_eq, comparator_15_eq, comparator_16_eq,
       comparator_17_eq, comparator_18_eq, comparator_19_eq, comparator_20_eq, comparator_21_eq,
       comparator_22_eq, comparator_23_eq, comparator_24_eq, comparator_25_eq, comparator_26_eq,
       comparator_27_eq, comparator_28_eq, comparator_29_eq, comparator_30_eq, comparator_31_eq,
       comparator_32_eq, comparator_33_eq, comparator_34_eq, comparator_35_eq, comparator_36_eq,
       comparator_37_eq, comparator_38_eq, comparator_39_eq, comparator_40_eq, comparator_41_eq,
       comparator_42_eq, comparator_43_eq, comparator_44_eq, comparator_45_eq, comparator_46_eq, IT1, JT1,
       RT1;
  wire [4:0] D1, S1, T1;
  wire [5:0] fun2, OP2;
  wire [10:0] AI2;
  wire [15:0] main_1_ra_value, main_1_s0_value, main_1_s1_value, main_1_s2_value;
  wire [25:0] TA2;
  wire [31:0] ai_t, bit_extender_2_out, bit_extender_7_out, bit_extender_8_out, bit_extender_9_out, d_t, FUN,
       ity, jty, op_t, rty, s_t, t_t, ta_t;
  wire [31:16] main_1_sp_value;

  or or_1 (JT1, comparator_9_eq, comparator_10_eq);
  Clock clock_1 (.out(clock_1_out));
  cpu_main main_1 (
    .INSTRUCTION(out_10), .CLOCK(clock_1_out), .FETCH_ADDRESS(Requested_Address),
    .s0_Value({main_1_s0_value, _1_Value}), .s1_Value({main_1_s1_value, _2_Value}),
    .s2_Value({main_1_s2_value, _3_Value}), .ra_Value({main_1_ra_value, _6_i_e__ra_Value}),
    .sp_Value({main_1_sp_value, _7_i_e__sp_Value}));
  Counter #(.width(32), .max('hffffffff)) counter_1 (
    .Q(Time_Step), .clk(clock_1_out));  // open: load, D, count, carry, clr
  Comparator #(.width(4)) comparator_1 (
    .a(Requested_Instruction[3:0]), .b(4'b0000), .eq(comparator_1_eq));  // open: gt, lt
  Comparator #(.width(4)) comparator_2 (
    .a(Requested_Instruction[3:0]), .b(4'b0001), .eq(comparator_2_eq));  // open: gt, lt
  Comparator #(.width(4)) comparator_3 (
    .a(Requested_Instruction[3:0]), .b(4'b0010), .eq(comparator_3_eq));  // open: gt, lt
  Comparator #(.width(4)) comparator_4 (
    .a(Requested_Instruction[3:0]), .b(4'b0011), .eq(comparator_4_eq));  // open: gt, lt
  Comparator #(.width(4)) comparator_5 (
    .a(Requested_Instruction[3:0]), .b(4'b0100), .eq(comparator_5_eq));  // open: gt, lt
  Comparator #(.width(4)) comparator_6 (
    .a(Requested_Instruction[3:0]), .b(4'b1000), .eq(comparator_6_eq));  // open: gt, lt
  Comparator #(.width(3)) comparator_7 (.a(Requested_Instruction[15:13]), .b(3'b000), .eq(RT1));  // open: gt, lt
  Comparator #(.width(3)) comparator_8 (
    .a(Requested_Instruction[15:13]), .b(3'b001), .eq(comparator_8_eq));  // open: gt, lt
  Comparator #(.width(3)) comparator_9 (
    .a(Requested_Instruction[15:13]), .b(3'b010), .eq(comparator_9_eq));  // open: gt, lt
  Comparator #(.width(3)) comparator_10 (
    .a(Requested_Instruction[15:13]), .b(3'b011), .eq(comparator_10_eq));  // open: gt, lt
  Comparator #(.width(3)) comparator_11 (
    .a(Requested_Instruction[15:13]), .b(3'b100), .eq(comparator_11_eq));  // open: gt, lt
  Comparator #(.width(3)) comparator_12 (
    .a(Requested_Instruction[15:13]), .b(3'b101), .eq(comparator_12_eq));  // open: gt, lt
  Comparator #(.width(3)) comparator_13 (
    .a(Requested_Instruction[15:13]), .b(3'b110), .eq(comparator_13_eq));  // open: gt, lt
  Comparator #(.width(3)) comparator_14 (
    .a(Requested_Instruction[15:13]), .b(3'b111), .eq(comparator_14_eq));  // open: gt, lt
  Multiplexer #(.width(6), .enable("false")) multiplexer_1 (
    .in1(6'b100000), .out(fun2), .sel(comparator_1_eq));  // open: in0
  Multiplexer #(.width(6), .enable("false")) multiplexer_2 (
    .in1(6'b100010), .out(fun2), .sel(comparator_2_eq));  // open: in0
  Multiplexer #(.width(6), .enable("false")) multiplexer_3 (
    .in1(6'b100100), .out(fun2), .sel(comparator_3_eq));  // open: in0
  Multiplexer #(.width(6), .enable("false")) multiplexer_4 (
    .in1(6'b100101), .out(fun2), .sel(comparator_4_eq));  // open: in0
  Multiplexer #(.width(6), .enable("false")) multiplexer_5 (
    .in1(6'b101010), .out(fun2), .sel(comparator_5_eq));  // open: in0
  Multiplexer #(.width(6), .enable("false")) multiplexer_6 (
    .in1(6'b001000), .out(fun2), .sel(comparator_6_eq));  // open: in0
  or or_2 (IT1, comparator_8_eq, comparator_11_eq, comparator_12_eq, comparator_13_eq, comparator_14_eq);
  assign FUN = {{26{1'b0}}, fun2};  // Bit_Extender bit_extender_1
  assign bit_extender_2_out = {{26{1'b0}}, OP2};  // Bit_Extender bit_extender_2
  assign ai_t = {{21{1'b0}}, AI2};  // Bit_Extender bit_extender_3
  assign ta_t = {{6{1'b0}}, TA2};  // Bit_Extender bit_extender_4
  Multiplexer #(.width(32), .enable("false")) multiplexer_7 (.in1(rty), .out(out_10), .sel(RT1));  // open: in0
  // Probe on Requested_Address
  Shifter #(.width(32)) shifter_1 (.in(bit_extender_2_out), .\dist (5'b11010), .out(op_t));
  assign rty = FUN | d_t | t_t | s_t | op_t;  // OR_Gate or_3, 32 bits wide
  Comparator #(.width(3)) comparator_15 (
    .a(Requested_Instruction[15:13]), .b(3'b000), .eq(comparator_15_eq));  // open: gt, lt
  Comparator #(.width(3)) comparator_16 (
    .a(Requested_Instruction[15:13]), .b(3'b111), .eq(comparator_16_eq));  // open: gt, lt
  Comparator #(.width(3)) comparator_17 (
    .a(Requested_Instruction[15:13]), .b(3'b110), .eq(comparator_17_eq));  // open: gt, lt
  Comparator #(.width(3)) comparator_18 (
    .a(Requested_Instruction[15:13]), .b(3'b101), .eq(comparator_18_eq));  // open: gt, lt
  Comparator #(.width(3)) comparator_19 (
    .a(Requested_Instruction[15:13]), .b(3'b100), .eq(comparator_19_eq));  // open: gt, lt
  Comparator #(.width(3)) comparator_20 (
    .a(Requested_Instruction[15:13]), .b(3'b011), .eq(comparator_20_eq));  // open: gt, lt
  Comparator #(.width(3)) comparator_21 (
    .a(Requested_Instruction[15:13]), .b(3'b010), .eq(comparator_21_eq));  // open: gt, lt
  Comparator #(.width(3)) comparator_22 (
    .a(Requested_Instruction[15:13]), .b(3'b001), .eq(comparator_22_eq));  // open: gt, lt
  Multiplexer #(.width(32), .enable("false")) multiplexer_8 (.in1(ity), .out(out_10), .sel(IT1));  // open: in0
  Multiplexer #(.width(6), .enable("false")) multiplexer_9 (
    .in1({6{1'b0}}), .out(OP2), .sel(comparator_15_eq));  // open: in0
  Multiplexer #(.width(6), .enable("false")) multiplexer_10 (
    .in1(6'b001000), .out(OP2), .sel(comparator_16_eq));  // open: in0
  Multiplexer #(.width(6), .enable("false")) multiplexer_11 (
    .in1(6'b000100), .out(OP2), .sel(comparator_17_eq));  // open: in0
  Multiplexer #(.width(6), .enable("false")) multiplexer_12 (
    .in1(6'b101011), .out(OP2), .sel(comparator_18_eq));  // open: in0
  Multiplexer #(.width(6), .enable("false")) multiplexer_13 (
    .in1(6'b100011), .out(OP2), .sel(comparator_19_eq));  // open: in0
  Multiplexer #(.width(6), .enable("false")) multiplexer_14 (
    .in1(6'b000011), .out(OP2), .sel(comparator_20_eq));  // open: in0
  Multiplexer #(.width(6), .enable("false")) multiplexer_15 (
    .in1(6'b000010), .out(OP2), .sel(comparator_21_eq));  // open: in0
  Multiplexer #(.width(6), .enable("false")) multiplexer_16 (
    .in1(6'b001010), .out(OP2), .sel(comparator_22_eq));  // open: in0
  Multiplexer #(.width(32), .enable("false")) multiplexer_17 (.in1(jty), .out(out_10), .sel(JT1));  // open: in0
  ROM #(.addrWidth(24), .dataWidth(16)) rom_1 (
    .addr(Requested_Address[25:2]), .data(Requested_Instruction));  // open: sel
  // Probe on Requested_Instruction
  assign ity = ai_t | t_t | s_t | op_t;  // OR_Gate or_4, 32 bits wide
  assign jty = ta_t | op_t;  // OR_Gate or_5, 32 bits wide
  assign AI2 = {{4{1'b0}}, Requested_Instruction[6:0]};  // Bit_Extender bit_extender_5
  assign TA2 = {{13{1'b0}}, Requested_Instruction[12:0]};  // Bit_Extender bit_extender_6
  Comparator #(.width(3)) comparator_23 (
    .a(Requested_Instruction[6:4]), .b(3'b000), .eq(comparator_23_eq));  // open: gt, lt
  Comparator #(.width(3)) comparator_24 (
    .a(Requested_Instruction[6:4]), .b(3'b001), .eq(comparator_24_eq));  // open: gt, lt
  Comparator #(.width(3)) comparator_25 (
    .a(Requested_Instruction[6:4]), .b(3'b010), .eq(comparator_25_eq));  // open: gt, lt
  Comparator #(.width(3)) comparator_26 (
    .a(Requested_Instruction[6:4]), .b(3'b011), .eq(comparator_26_eq));  // open: gt, lt
  Comparator #(.width(3)) comparator_27 (
    .a(Requested_Instruction[6:4]), .b(3'b100), .eq(comparator_27_eq));  // open: gt, lt
  Comparator #(.width(3)) comparator_28 (
    .a(Requested_Instruction[6:4]), .b(3'b101), .eq(comparator_28_eq));  // open: gt, lt
  Comparator #(.width(3)) comparator_29 (
    .a(Requested_Instruction[6:4]), .b(3'b110), .eq(comparator_29_eq));  // open: gt, lt
  Comparator #(.width(3)) comparator_30 (
    .a(Requested_Instruction[6:4]), .b(3'b111), .eq(comparator_30_eq));  // open: gt, lt
  Comparator #(.width(3)) comparator_31 (
    .a(Requested_Instruction[12:10]), .b(3'b000), .eq(comparator_31_eq));  // open: gt, lt
  Comparator #(.width(3)) comparator_32 (
    .a(Requested_Instruction[12:10]), .b(3'b001), .eq(comparator_32_eq));  // open: gt, lt
  Comparator #(.width(3)) comparator_33 (
    .a(Requested_Instruction[12:10]), .b(3'b010), .eq(comparator_33_eq));  // open: gt, lt
  Comparator #(.width(3)) comparator_34 (
    .a(Requested_Instruction[12:10]), .b(3'b011), .eq(comparator_34_eq));  // open: gt, lt
  Comparator #(.width(3)) comparator_35 (
    .a(Requested_Instruction[12:10]), .b(3'b100), .eq(comparator_35_eq));  // open: gt, lt
  Comparator #(.width(3)) comparator_36 (
    .a(Requested_Instruction[12:10]), .b(3'b101), .eq(comparator_36_eq));  // open: gt, lt
  Comparator #(.width(3)) comparator_37 (
    .a(Requested_Instruction[12:10]), .b(3'b110), .eq(comparator_37_eq));  // open: gt, lt
  Comparator #(.width(3)) comparator_38 (
    .a(Requested_Instruction[12:10]), .b(3'b111), .eq(comparator_38_eq));  // open: gt, lt
  Multiplexer #(.width(5), .enable("false")) multiplexer_18 (
    .in1({5{1'b0}}), .out(D1), .sel(comparator_23_eq));  // open: in0
  Multiplexer #(.width(5), .enable("false")) multiplexer_19 (
    .in1(5'b10000), .out(D1), .sel(comparator_24_eq));  // open: in0
  Multiplexer #(.width(5), .enable("false")) multiplexer_20 (
    .in1(5'b10001), .out(D1), .sel(comparator_25_eq));  // open: in0
  Multiplexer #(.width(5), .enable("false")) multiplexer_21 (
    .in1(5'b10010), .out(D1), .sel(comparator_26_eq));  // open: in0
  Multiplexer #(.width(5), .enable("false")) multiplexer_22 (
    .in1(5'b00100), .out(D1), .sel(comparator_27_eq));  // open: in0
  Multiplexer #(.width(5), .enable("false")) multiplexer_23 (
    .in1(5'b00101), .out(D1), .sel(comparator_28_eq));  // open: in0
  Multiplexer #(.width(5), .enable("false")) multiplexer_24 (
    .in1(5'b11101), .out(D1), .sel(comparator_29_eq));  // open: in0
  Multiplexer #(.width(5), .enable("false")) multiplexer_25 (
    .in1({5{1'b1}}), .out(D1), .sel(comparator_30_eq));  // open: in0
  Multiplexer #(.width(5), .enable("false")) multiplexer_26 (
    .in1({5{1'b0}}), .out(S1), .sel(comparator_31_eq));  // open: in0
  Multiplexer #(.width(5), .enable("false")) multiplexer_27 (
    .in1(5'b10000), .out(S1), .sel(comparator_32_eq));  // open: in0
  Multiplexer #(.width(5), .enable("false")) multiplexer_28 (
    .in1(5'b10001), .out(S1), .sel(comparator_33_eq));  // open: in0
  Multiplexer #(.width(5), .enable("false")) multiplexer_29 (
    .in1(5'b10010), .out(S1), .sel(comparator_34_eq));  // open: in0
  Multiplexer #(.width(5), .enable("false")) multiplexer_30 (
    .in1(5'b00100), .out(S1), .sel(comparator_35_eq));  // open: in0
  Multiplexer #(.width(5), .enable("false")) multiplexer_31 (
    .in1(5'b00101), .out(S1), .sel(comparator_36_eq));  // open: in0
  Multiplexer #(.width(5), .enable("false")) multiplexer_32 (
    .in1(5'b11101), .out(S1), .sel(comparator_37_eq));  // open: in0
  Multiplexer #(.width(5), .enable("false")) multiplexer_33 (
    .in1({5{1'b1}}), .out(S1), .sel(comparator_38_eq));  // open: in0
  Comparator #(.width(3)) comparator_39 (
    .a(Requested_Instruction[9:7]), .b(3'b000), .eq(comparator_39_eq));  // open: gt, lt
  Comparator #(.width(3)) comparator_40 (
    .a(Requested_Instruction[9:7]), .b(3'b001), .eq(comparator_40_eq));  // open: gt, lt
  Comparator #(.width(3)) comparator_41 (
    .a(Requested_Instruction[9:7]), .b(3'b010), .eq(comparator_41_eq));  // open: gt, lt
  Comparator #(.width(3)) comparator_42 (
    .a(Requested_Instruction[9:7]), .b(3'b011), .eq(comparator_42_eq));  // open: gt, lt
  Comparator #(.width(3)) comparator_43 (
    .a(Requested_Instruction[9:7]), .b(3'b100), .eq(comparator_43_eq));  // open: gt, lt
  Comparator #(.width(3)) comparator_44 (
    .a(Requested_Instruction[9:7]), .b(3'b101), .eq(comparator_44_eq));  // open: gt, lt
  Comparator #(.width(3)) comparator_45 (
    .a(Requested_Instruction[9:7]), .b(3'b110), .eq(comparator_45_eq));  // open: gt, lt
  Comparator #(.width(3)) comparator_46 (
    .a(Requested_Instruction[9:7]), .b(3'b111), .eq(comparator_46_eq));  // open: gt, lt
  assign bit_extender_7_out = {{27{1'b0}}, D1};  // Bit_Extender bit_extender_7
  assign bit_extender_8_out = {{27{1'b0}}, T1};  // Bit_Extender bit_extender_8
  assign bit_extender_9_out = {{27{1'b0}}, S1};  // Bit_Extender bit_extender_9
  Multiplexer #(.width(5), .enable("false")) multiplexer_34 (
    .in1({5{1'b0}}), .out(T1), .sel(comparator_39_eq));  // open: in0
  Multiplexer #(.width(5), .enable("false")) multiplexer_35 (
    .in1(5'b10000), .out(T1), .sel(comparator_40_eq));  // open: in0
  Multiplexer #(.width(5), .enable("false")) multiplexer_36 (
    .in1(5'b10001), .out(T1), .sel(comparator_41_eq));  // open: in0
  Multiplexer #(.width(5), .enable("false")) multiplexer_37 (
    .in1(5'b10010), .out(T1), .sel(comparator_42_eq));  // open: in0
  Multiplexer #(.width(5), .enable("false")) multiplexer_38 (
    .in1(5'b00100), .out(T1), .sel(comparator_43_eq));  // open: in0
  Multiplexer #(.width(5), .enable("false")) multiplexer_39 (
    .in1(5'b00101), .out(T1), .sel(comparator_44_eq));  // open: in0
  Multiplexer #(.width(5), .enable("false")) multiplexer_40 (
    .in1(5'b11101), .out(T1), .sel(comparator_45_eq));  // open: in0
  Multiplexer #(.width(5), .enable("false")) multiplexer_41 (
    .in1({5{1'b1}}), .out(T1), .sel(comparator_46_eq));  // open: in0
  Shifter #(.width(32)) shifter_2 (.in(bit_extender_7_out), .\dist (5'b01011), .out(d_t));
  Shifter #(.width(32)) shifter_3 (.in(bit_extender_8_out), .\dist (5'b10000), .out(t_t));
  Shifter #(.width(32)) shifter_4 (.in(bit_extender_9_out), .\dist (5'b10101), .out(s_t));

  assign Requested_Instruction_2 = Requested_Instruction;

  // Other names for the same wires on the sheet: fetch_addr[31:0] = Requested_Address; ins[31:0] = out_10;
  //   AI[6:0] = Requested_Instruction[6:0]; fun_t[3:0] = Requested_Instruction[3:0]; q[15:0] = Requested_Instruction;
  //   TA[12:0] = Requested_Instruction[12:0]; D[2:0] = Requested_Instruction[6:4];
  //   T[2:0] = Requested_Instruction[9:7]; S[2:0] = Requested_Instruction[12:10];
  //   OP[2:0] = Requested_Instruction[15:13]

  // Notes on the sheet:
  //   YOUR CPU SHOULD FIT IN HERE!
  //   16 - BIT SINGLE CYCLE MIPS PROCESSOR
  //   Instruction Memory
  //   SUBMITTED BY:
  //   contents of rom_1 (hex, n*v repeats v):
  //   e08a a08a 810a c50a 124*0 1c08 347*0 100 4*0 201 2 0 2 0 0 0 5
  //   SUMUKHA PK    16CO145
  //   PRAJVAL M     16CO234
  //   INSTRUCTIONS GO HERE
endmodule
