// Logisim project cpu.circ as structural Verilog: 1 circuit, main circuit main
module main (
  input  [31:0] INSTRUCTION,
  input  CLOCK,
  output [31:0] FETCH_ADDRESS,
  output [31:0] s0_Value,
  output [31:0] s1_Value,
  output [31:0] s2_Value,
  output [31:0] ra_Value,
  output [31:0] sp_Value
);

  wire add, addi, addiu, addu, ALU_Equal, ALU_Overflow, ALUSrc, \and , and_14_out, and_15_out, and_16_out,
       and_18_out, and_19_out, and_20_out, andi, beq, bne, bov, Branch, comparator_16_eq, comparator_17_eq,
       comparator_18_eq, comparator_19_eq, comparator_20_eq, comparator_21_eq, comparator_22_eq,
       comparator_23_eq, comparator_24_eq, comparator_25_eq, comparator_26_eq, comparator_27_eq,
       comparator_28_eq, ExtOp, j, jal, jalr, jr, Kill, lui, lw, MemWrite, not_1_out, not_2_out, not_3_out,
       not_5_out, not_6_out, not_7_out, not_8_out, not_9_out, not_10_out, not_11_out, \or , or_1_out,
       or_2_out, or_3_out, or_4_out, or_7_out, or_8_out, or_9_out, or_10_out, or_11_out, or_12_out,
       or_13_out, or_14_out, or_16_out, or_17_out, or_18_out, ori, R_type, RegWrite, sll, slt, slti, sltiu,
       sltu, sra, srl, sub, subu;
  wire [3:0] ALUctr, multiplexer_4_out, multiplexer_5_out, multiplexer_7_out, multiplexer_8_out,
       multiplexer_9_out, multiplexer_11_out, multiplexer_14_out, multiplexer_16_out, multiplexer_17_out,
       multiplexer_19_out;
  wire [4:0] multiplexer_2_out, multiplexer_3_out;
  wire [5:0] funct, opcode;
  wire [15:6] immediate;
  wire [25:16] jump_address;
  wire [27:0] adder_3_out, bit_extender_2_out;
  wire [31:0] adder_2_out, ALU_Output, bit_extender_1_out, bit_extender_3_out, bit_extender_4_out,
       bit_extender_5_out, main_2_result, main_3_p5, multiplexer_1_out, multiplexer_6_out,
       multiplexer_10_out, multiplexer_13_out, multiplexer_15_out, multiplexer_18_out, multiplexer_23_out,
       next_PC, PC_4, ReadData1, ReadData2, shifter_1_out, shifter_2_out, shifter_3_out, shifter_4_out,
       WriteData;

  Register #(.width(32)) PC (.D(next_PC), .Q(FETCH_ADDRESS), .clk(CLOCK));  // open: en, clr
  Multiplexer #(.width(32)) multiplexer_1 (
    .in0(INSTRUCTION), .in1({32{1'b0}}), .out(multiplexer_1_out), .sel(Kill));  // open: en
  Comparator #(.width(6), .mode("unsigned")) comparator_1 (.a(opcode), .b({6{1'b0}}), .eq(R_type));  // open: gt, lt
  Comparator #(.width(6), .mode("unsigned")) comparator_2 (.a(opcode), .b(6'b001000), .eq(addi));  // open: gt, lt
  Comparator #(.width(6), .mode("unsigned")) comparator_3 (.a(opcode), .b(6'b001001), .eq(addiu));  // open: gt, lt
  Comparator #(.width(6), .mode("unsigned")) comparator_4 (.a(opcode), .b(6'b001100), .eq(andi));  // open: gt, lt
  Comparator #(.width(6), .mode("unsigned")) comparator_5 (.a(opcode), .b(6'b000100), .eq(beq));  // open: gt, lt
  Comparator #(.width(6), .mode("unsigned")) comparator_6 (.a(opcode), .b(6'b000101), .eq(bne));  // open: gt, lt
  Comparator #(.width(6), .mode("unsigned")) comparator_7 (.a(opcode), .b(6'b000110), .eq(bov));  // open: gt, lt
  Comparator #(.width(6), .mode("unsigned")) comparator_8 (.a(opcode), .b(6'b000010), .eq(j));  // open: gt, lt
  Comparator #(.width(6), .mode("unsigned")) comparator_9 (.a(opcode), .b(6'b000011), .eq(jal));  // open: gt, lt
  Comparator #(.width(6), .mode("unsigned")) comparator_10 (.a(opcode), .b(6'b001111), .eq(lui));  // open: gt, lt
  Comparator #(.width(6), .mode("unsigned")) comparator_11 (.a(opcode), .b(6'b100011), .eq(lw));  // open: gt, lt
  Comparator #(.width(6), .mode("unsigned")) comparator_12 (.a(opcode), .b(6'b001101), .eq(ori));  // open: gt, lt
  Comparator #(.width(6), .mode("unsigned")) comparator_13 (.a(opcode), .b(6'b001010), .eq(slti));  // open: gt, lt
  Comparator #(.width(6), .mode("unsigned")) comparator_14 (.a(opcode), .b(6'b001011), .eq(sltiu));  // open: gt, lt
  Comparator #(.width(6), .mode("unsigned")) comparator_15 (.a(opcode), .b(6'b101011), .eq(MemWrite));  // open: gt, lt
  Register #(.width(32)) A (
    .D(multiplexer_1_out), .Q({opcode, jump_address, immediate, funct}), .clk(CLOCK));  // open: en, clr
  Comparator #(.width(6), .mode("unsigned")) comparator_16 (
    .a(funct), .b(6'b100000), .eq(comparator_16_eq));  // open: gt, lt
  Comparator #(.width(6), .mode("unsigned")) comparator_17 (
    .a(funct), .b(6'b100001), .eq(comparator_17_eq));  // open: gt, lt
  Comparator #(.width(6), .mode("unsigned")) comparator_18 (
    .a(funct), .b(6'b100100), .eq(comparator_18_eq));  // open: gt, lt
  Comparator #(.width(6), .mode("unsigned")) comparator_19 (
    .a(funct), .b(6'b001000), .eq(comparator_19_eq));  // open: gt, lt
  Comparator #(.width(6), .mode("unsigned")) comparator_20 (
    .a(funct), .b(6'b001001), .eq(comparator_20_eq));  // open: gt, lt
  Comparator #(.width(6), .mode("unsigned")) comparator_21 (
    .a(funct), .b(6'b100101), .eq(comparator_21_eq));  // open: gt, lt
  Comparator #(.width(6), .mode("unsigned")) comparator_22 (
    .a(funct), .b(6'b101010), .eq(comparator_22_eq));  // open: gt, lt
  Comparator #(.width(6), .mode("unsigned")) comparator_23 (
    .a(funct), .b(6'b101011), .eq(comparator_23_eq));  // open: gt, lt
  Comparator #(.width(6), .mode("unsigned")) comparator_24 (
    .a(funct), .b({6{1'b0}}), .eq(comparator_24_eq));  // open: gt, lt
  Comparator #(.width(6), .mode("unsigned")) comparator_25 (
    .a(funct), .b(6'b000011), .eq(comparator_25_eq));  // open: gt, lt
  Comparator #(.width(6), .mode("unsigned")) comparator_26 (
    .a(funct), .b(6'b000010), .eq(comparator_26_eq));  // open: gt, lt
  Comparator #(.width(6), .mode("unsigned")) comparator_27 (
    .a(funct), .b(6'b100010), .eq(comparator_27_eq));  // open: gt, lt
  Comparator #(.width(6), .mode("unsigned")) comparator_28 (
    .a(funct), .b(6'b100011), .eq(comparator_28_eq));  // open: gt, lt
  and and_1 (add, comparator_16_eq, R_type);
  and and_2 (addu, comparator_17_eq, R_type);
  and and_3 (\and , comparator_18_eq, R_type);
  and and_4 (jr, comparator_19_eq, R_type);
  and and_5 (jalr, comparator_20_eq, R_type);
  and and_6 (\or , comparator_21_eq, R_type);
  and and_7 (slt, comparator_22_eq, R_type);
  and and_8 (sltu, comparator_23_eq, R_type);
  and and_9 (sll, comparator_24_eq, R_type);
  and and_10 (sra, comparator_25_eq, R_type);
  and and_11 (srl, comparator_26_eq, R_type);
  and and_12 (sub, comparator_27_eq, R_type);
  and and_13 (subu, comparator_28_eq, R_type);
  Multiplexer #(.width(5)) multiplexer_2 (
    .in0(jump_address[20:16]), .in1(immediate[15:11]), .out(multiplexer_2_out), .sel(R_type));  // open: en
  Multiplexer #(.width(5)) multiplexer_3 (
    .in0(multiplexer_2_out), .in1({5{1'b1}}), .out(multiplexer_3_out), .sel(or_1_out));  // open: en
  or or_1 (or_1_out, jal, jalr);
  Adder #(.width(32)) adder_1 (.a(FETCH_ADDRESS), .b(32'h4), .out(PC_4));  // open: cin, cout
  assign bit_extender_1_out = {{16{immediate[15]}}, {immediate, funct}};  // Bit_Extender bit_extender_1
  Shifter #(.width(32)) shifter_1 (.in(bit_extender_1_out), .\dist (5'b00010), .out(shifter_1_out));
  or or_2 (or_2_out, beq, bov, bne);
  Multiplexer #(.width(4)) multiplexer_4 (
    .in0(4'b0000), .in1(4'b1100), .out(multiplexer_4_out), .sel(or_3_out));  // open: en
  or or_3 (or_3_out, sltu, sltiu);
  Adder #(.width(32)) adder_2 (.a(FETCH_ADDRESS), .b(shifter_1_out), .out(adder_2_out));  // open: cin, cout
  or or_4 (or_4_out, and_14_out, and_15_out, and_16_out);
  Adder #(.width(32)) adder_3 (
    .a(FETCH_ADDRESS), .b(32'h4), .out({shifter_2_out[31:28], adder_3_out}));  // open: cin, cout
  assign bit_extender_2_out = {{2{1'b0}}, {jump_address, immediate, funct}};  // Bit_Extender bit_extender_2
  regfile_main main_1 (
    .Read_Register_1(jump_address[25:21]), .Read_Register_2(jump_address[20:16]),
    .Write_Register(multiplexer_3_out), .Write_Data(WriteData), .Write_Enable(RegWrite), .Clock(CLOCK),
    .Read_Data_1(ReadData1), .Read_Data_2(ReadData2), ._1_Value(s0_Value), ._2_Value(s1_Value),
    ._3_Value(s2_Value), ._6_Value(ra_Value), ._7_Value(sp_Value));
  or or_5 (Branch, beq, bov, bne);
  not not_1 (not_1_out, R_type);
  not not_2 (not_2_out, or_2_out);
  or or_6 (ExtOp, addi, addiu, slti);
  Multiplexer #(.width(4)) multiplexer_5 (
    .in0(multiplexer_4_out), .in1(4'b1011), .out(multiplexer_5_out), .sel(or_7_out));  // open: en
  or or_7 (or_7_out, slt, slti);
  Multiplexer #(.width(32)) multiplexer_6 (
    .in0(PC_4), .in1(adder_2_out), .out(multiplexer_6_out), .sel(or_4_out));  // open: en
  and and_14 (and_14_out, beq, ALU_Equal);
  and and_15 (and_15_out, bne, not_3_out);
  not not_3 (not_3_out, ALU_Equal);
  and and_16 (and_16_out, bov, ALU_Overflow);
  Shifter #(.width(28)) shifter_2 (.in(bit_extender_2_out), .\dist (5'b00010), .out(shifter_2_out[27:0]));
  and and_17 (ALUSrc, not_1_out, not_2_out);
  or or_8 (or_8_out, beq, bov, bne, j, jr, MemWrite);
  not not_4 (RegWrite, or_8_out);
  Multiplexer #(.width(4)) multiplexer_7 (
    .in0(multiplexer_5_out), .in1(4'b1010), .out(multiplexer_7_out), .sel(or_9_out));  // open: en
  or or_9 (or_9_out, \or , ori);
  Multiplexer #(.width(4)) multiplexer_8 (
    .in0(multiplexer_7_out), .in1(4'b1001), .out(multiplexer_8_out), .sel(or_10_out));  // open: en
  or or_10 (or_10_out, \and , andi);
  Subtractor #(.width(32)) subtractor_1 (.b(32'h4));  // open: a, out, bin, bout
  Multiplexer #(.width(4)) multiplexer_9 (
    .in0(multiplexer_8_out), .in1(4'b1000), .out(multiplexer_9_out), .sel(subu));  // open: en
  Multiplexer #(.width(32)) multiplexer_10 (
    .in0(multiplexer_6_out), .in1(shifter_2_out), .out(multiplexer_10_out), .sel(or_11_out));  // open: en
  or or_11 (or_11_out, jal, j);
  assign bit_extender_3_out = {{16{1'b0}}, {immediate, funct}};  // Bit_Extender bit_extender_3
  assign bit_extender_4_out = {{16{immediate[15]}}, {immediate, funct}};  // Bit_Extender bit_extender_4
  or or_12 (or_12_out, and_18_out, and_19_out, and_20_out);
  and and_18 (and_18_out, beq, ALU_Equal);
  and and_19 (and_19_out, bne, not_5_out);
  Multiplexer #(.width(4)) multiplexer_11 (
    .in0(multiplexer_9_out), .in1(4'b0111), .out(multiplexer_11_out), .sel(sub));  // open: en
  Multiplexer #(.width(32)) multiplexer_12 (
    .in0(multiplexer_10_out), .in1(ReadData1), .out(next_PC), .sel(or_13_out));  // open: en
  or or_13 (or_13_out, jr, jalr);
  Multiplexer #(.width(32)) multiplexer_13 (
    .in0(bit_extender_3_out), .in1(bit_extender_4_out), .out(multiplexer_13_out), .sel(ExtOp));  // open: en
  or or_14 (or_14_out, jalr, j, jal, jr);
  and and_20 (and_20_out, bov, ALU_Overflow);
  not not_5 (not_5_out, ALU_Equal);
  Multiplexer #(.width(4)) multiplexer_14 (
    .in0(multiplexer_11_out), .in1(4'b0010), .out(multiplexer_14_out), .sel(sra));  // open: en
  Multiplexer #(.width(32)) multiplexer_15 (
    .in0(multiplexer_13_out), .in1(shifter_3_out), .out(multiplexer_15_out), .sel(lui));  // open: en
  Shifter #(.width(32)) shifter_3 (.in(multiplexer_13_out), .\dist (5'b10110), .out(shifter_3_out));
  or or_15 (Kill, or_14_out, or_12_out);
  Multiplexer #(.width(4)) multiplexer_16 (
    .in0(multiplexer_14_out), .in1(4'b0001), .out(multiplexer_16_out), .sel(srl));  // open: en
  Multiplexer #(.width(4)) multiplexer_17 (
    .in0(multiplexer_16_out), .in1(4'b0000), .out(multiplexer_17_out), .sel(sll));  // open: en
  or or_16 (or_16_out, addu, lui, addiu);
  Multiplexer #(.width(32)) multiplexer_18 (
    .in0(ReadData2), .in1(multiplexer_15_out), .out(multiplexer_18_out), .sel(ALUSrc));  // open: en
  Multiplexer #(.width(4)) multiplexer_19 (
    .in0(multiplexer_17_out), .in1(4'b0110), .out(multiplexer_19_out), .sel(or_16_out));  // open: en
  or or_17 (or_17_out, add, bov, addi);
  LED led_1 (.in(ALU_Overflow));
  alu_main main_2 (
    .Switch(ALUctr), .X(ReadData1), .Equal(ALU_Equal), .Result(main_2_result),
    .Signed_Overflow(ALU_Overflow), .Y(multiplexer_18_out));
  Multiplexer #(.width(4)) multiplexer_20 (
    .in0(multiplexer_19_out), .in1(4'b0101), .out(ALUctr), .sel(or_17_out));  // open: en
  assign bit_extender_5_out = {{16{1'b0}}, {immediate, funct}};  // Bit_Extender bit_extender_5
  Shifter #(.width(32)) shifter_4 (.in(bit_extender_5_out), .\dist (5'b10000), .out(shifter_4_out));
  Multiplexer #(.width(32)) multiplexer_21 (
    .in0(main_2_result), .in1(shifter_4_out), .out(ALU_Output), .sel(lui));  // open: en
  Multiplexer #(.width(32)) multiplexer_22 ();  // open: in0, in1, out, sel, en
  not not_6 (not_6_out, opcode[5]);
  not not_7 (not_7_out, opcode[4]);
  not not_8 (not_8_out, opcode[2]);
  not not_9 (not_9_out, opcode[3]);
  not not_10 (not_10_out, opcode[0]);
  not not_11 (not_11_out, opcode[1]);
  Multiplexer #(.width(32)) multiplexer_23 (
    .in0(ALU_Output), .in1(main_3_p5), .out(multiplexer_23_out), .sel(lw));  // open: en
  // mem_main main_3: pin names not known; wires that end beside it: ALU_Output, ReadData2, MemWrite, CLOCK, main_3_p5
  // AND_Gate and_21 has open pins: in0=not_6_out, in1=not_7_out, in2=not_9_out, in3=not_8_out, in4=not_11_out, in5=not_10_out, out=open
  Multiplexer #(.width(32)) multiplexer_24 (
    .in0(multiplexer_23_out), .in1(FETCH_ADDRESS), .out(WriteData), .sel(or_18_out));  // open: en
  or or_18 (or_18_out, jal, jalr);

  // Other names for the same wires on the sheet: clk = CLOCK; fetch_addr[31:0] = FETCH_ADDRESS; MemtoReg = lw;
  //   ra[31:0] = ra_Value; RegDst = R_type; s0[31:0] = s0_Value; s1[31:0] = s1_Value; s2[31:0] = s2_Value;
  //   sp[31:0] = sp_Value; sw = MemWrite; immediate[5:0] = funct; jump_address[15:0] = {immediate, funct};
  //   this_instruction[31:0] = {opcode, jump_address, immediate, funct}; shamt[4:0] = immediate[10:6];
  //   rd[4:0] = immediate[15:11]; rt[4:0] = jump_address[20:16]; rs[4:0] = jump_address[25:21]

  // Notes on the sheet:
  //   Output
  //   These are outputs/inputs from run.circ
  //   Inputs
  //   These are DEBUG/TEST outputs from your circuit.
endmodule
